// Logisim project B2_Group5_ALU.circ as structural Verilog: 2 circuits, main circuit main
module main (
  input  [2:0] CS2_CS1_CS0,
  input  [3:0] A3_A2_A1_A0,
  input  [3:0] B3_B2_B1_B0,
  output [3:0] S3_S2_S1_S0,
  output [3:0] C_S_V_Z
);

  ALU alu_1 (
    .CS2(CS2_CS1_CS0[2]), .CS1(CS2_CS1_CS0[1]), .CS0(CS2_CS1_CS0[0]), .A3(A3_A2_A1_A0[3]),
    .A2(A3_A2_A1_A0[2]), .A1(A3_A2_A1_A0[1]), .A0(A3_A2_A1_A0[0]), .B3(B3_B2_B1_B0[3]), .B2(B3_B2_B1_B0[2]),
    .B1(B3_B2_B1_B0[1]), .B0(B3_B2_B1_B0[0]), .S3(S3_S2_S1_S0[3]), .S2(S3_S2_S1_S0[2]), .S1(S3_S2_S1_S0[1]),
    .S0(S3_S2_S1_S0[0]), .C(C_S_V_Z[3]), .S(C_S_V_Z[2]), .V(C_S_V_Z[1]), .Z(C_S_V_Z[0]));
endmodule

// 4 Bit ALU
module ALU (
  input  CS2,
  input  CS1,
  input  CS0,
  input  A3,
  input  A2,
  input  A1,
  input  A0,
  input  B3,
  input  B2,
  input  B1,
  input  B0,
  output S3,
  output S2,
  output S1,
  output S0,
  output C,
  output S,
  output V,
  output Z
);

  wire n7404_1_p2, n7404_1_p4, n7404_1_p7, n7404_1_p9, n7404_1_p10, n7408_1_p3, n7408_1_p4, n7408_2_p3,
       n7408_2_p6, n7408_2_p11, n7408_2_p14, n7408_3_p3, n7408_3_p6, n7408_3_p11, n7408_3_p14, n7432_1_p1,
       n7432_1_p3, n7432_1_p6, n7432_1_p11, n7432_1_p14, n7432_2_p6, n7432_2_p11, n7483_1_p12, n7486_2_p3,
       n7486_2_p6, n7486_2_p11, n7486_2_p14;

  // _7404 7404_1: pin names not known; wires that end beside it: CS1, n7404_1_p2, CS0, n7404_1_p4, 1'b0, 1'b1, n7404_1_p7, Z, n7404_1_p9, n7404_1_p10
  // _7432 7432_1: pin names not known; wires that end beside it: n7432_1_p1, B3, n7432_1_p3, n7432_1_p1, B2, n7432_1_p6, 1'b0, 1'b1, n7432_1_p1, B1, n7432_1_p11, n7432_1_p1, B0, n7432_1_p14
  // _7408 7408_1: pin names not known; wires that end beside it: C, 1'b1, n7408_1_p3, n7408_1_p4, n7404_1_p2, n7404_1_p2, C, V, 1'b0
  // _7486 7486_1: pin names not known; wires that end beside it: 1'b0, 1'b1, n7404_1_p10, n7408_1_p3, n7408_1_p4
  // _7486 7486_2: pin names not known; wires that end beside it: n7404_1_p2, B3, n7486_2_p3, n7404_1_p2, B2, n7486_2_p6, 1'b0, 1'b1, n7404_1_p2, B1, n7486_2_p11, n7404_1_p2, B0, n7486_2_p14
  // _7408 7408_2: pin names not known; wires that end beside it: A3, n7432_1_p3, n7408_2_p3, n7432_1_p6, A2, n7408_2_p6, 1'b0, 1'b1, n7432_1_p14, A0, n7408_2_p11, A1, n7432_1_p11, n7408_2_p14
  // _7408 7408_3: pin names not known; wires that end beside it: n7404_1_p4, n7486_2_p3, n7408_3_p3, n7404_1_p4, n7486_2_p6, n7408_3_p6, 1'b0, 1'b1, n7404_1_p4, n7486_2_p14, n7408_3_p11, n7486_2_p11, n7404_1_p4, n7408_3_p14
  // _7432 7432_2: pin names not known; wires that end beside it: 1'b1, S0, n7404_1_p2, S1, n7404_1_p4, n7432_2_p6, n7432_1_p1, n7432_2_p6, S, S2, n7432_2_p11, n7432_2_p11, n7404_1_p7, 1'b0, CS1, CS0, n7404_1_p4
  // _7483 7483_1: pin names not known; wires that end beside it: n7408_2_p3, n7404_1_p9, n7404_1_p2, 1'b0, 1'b1, S2, n7408_3_p6, n7408_2_p6, n7408_3_p3, S, n7408_1_p3, n7483_1_p12, 1'b0, n7404_1_p2, 1'b0
  // _7483 7483_2: pin names not known; wires that end beside it: n7408_2_p14, n7404_1_p2, 1'b0, 1'b1, S0, n7408_3_p11, n7408_2_p11, n7408_3_p14, S1, n7483_1_p12, CS2, 1'b0, n7404_1_p2, 1'b0

  assign S3 = S;

  // Notes on the sheet:
  //   S1' + S0'
endmodule
