// Logisim project B2_Group5.circ as structural Verilog: 17 circuits, main circuit main
module main (
  input  [31:0] Number_A,
  input  [31:0] Number_B,
  output [31:0] Output,
  output Underflow,
  output Overflow
);

  Floating_Point_Adder floating_point_adder_1 (
    .UnderFlow(Underflow), .OverFlow(Overflow), .Number_A(Number_A), .Number_B(Number_B),
    .Rounded_Output(Output));
endmodule

module CompareExp (
  input  [9:0] Exponent_A,
  input  [9:0] Exponent_B,
  output [9:0] Exponent_Difference,
  output Exp_A___Exp_B,
  output [9:0] Larger_Exp
);

  wire [9:0] negator_1_out, subtractor_1_out;

  Subtractor #(.width(10)) subtractor_1 (
    .a(Exponent_B), .b(Exponent_A), .out(subtractor_1_out), .bin(1'b0), .bout(Exp_A___Exp_B));
  Negator #(.width(10)) negator_1 (.in(subtractor_1_out), .out(negator_1_out));
  Multiplexer #(.width(10), .disabled(0), .enable("false")) multiplexer_1 (
    .in0(Exponent_B), .in1(Exponent_A), .out(Larger_Exp), .sel(Exp_A___Exp_B));
  Multiplexer #(.width(10), .disabled(0), .enable("false")) multiplexer_2 (
    .in0(subtractor_1_out), .in1(negator_1_out), .out(Exponent_Difference), .sel(Exp_A___Exp_B));
endmodule

module CheckSign (
  input  sign,
  input  [31:0] frac_in,
  output [31:0] frac_out
);

  wire [31:0] negator_1_out;

  Negator #(.width(32)) negator_1 (.in(frac_in), .out(negator_1_out));
  _32bit_MUX u_32bit_mux_1 (.in_1(sign), .Input_0(frac_in), .Input_1(negator_1_out), .Output(frac_out));
endmodule

// Padding
module PaddingModule (
  input  [20:0] Fraction,
  input  [9:0] Exponent,
  output [31:0] out_3
);

  _10bit_OR u_10bit_or_1 (
    .in_1(Exponent[0]), .in_2(Exponent[1]), .in_3(Exponent[2]), .in_4(Exponent[3]), .in_5(Exponent[4]),
    .in_6(Exponent[5]), .in_7(Exponent[6]), .in_8(Exponent[7]), .in_9(Exponent[8]), .in_10(Exponent[9]),
    .\output (out_3[29]));

  assign {out_3[31:30], out_3[28:0]} = {2'b00, Fraction, {8{1'b0}}};
endmodule

// FPA
module Floating_Point_Adder (
  input  [31:0] Number_A,
  input  [31:0] Number_B,
  output UnderFlow,
  output OverFlow,
  output [31:0] Rounded_Output
);

  wire n74157_1_p1, n74157_1_p4, n74157_1_p7, nomalizatonmodule_1_at_least_one_1,
       signedsubtractor_1_msb__isneg;
  wire [9:0] compareexp_1_exponent_difference, compareexp_1_larger_exp, nomalizatonmodule_1_shamt,
       signedsubtractor_1_a_b;
  wire [31:0] addermodule_1_out_5, alignmodule_1_small_significand_out, n32bit_mux_1_output,
       n32bit_mux_2_output, nomalizatonmodule_1_normalized_op, paddingmodule_1_out_3, paddingmodule_2_out_3,
       roundingmodule_1_significantout;

  PaddingModule paddingmodule_1 (.Fraction(Number_A[20:0]), .Exponent(Number_A[30:21]), .out_3(paddingmodule_1_out_3));
  // _74157 74157_1: pin names not known; wires that end beside it: n74157_1_p1, Number_A[31], Number_B[31], n74157_1_p4, Number_B[31], Number_A[31], n74157_1_p7, 1'b0, 1'b1, 1'b0
  Overflow_Underflow overflow_underflow_1 (
    .At_least_one_1(nomalizatonmodule_1_at_least_one_1), .Normalized_exp(signedsubtractor_1_a_b),
    .Rounded_Exp(Rounded_Output[30:21]), .Underflow(UnderFlow), .Overflow(OverFlow),
    ._11th_bit__From_exp_subt(signedsubtractor_1_msb__isneg));
  CompareExp compareexp_1 (
    .Exponent_Difference(compareexp_1_exponent_difference), .Exp_A___Exp_B(n74157_1_p1),
    .Exponent_A(Number_A[30:21]), .Exponent_B(Number_B[30:21]), .Larger_Exp(compareexp_1_larger_exp));
  _32bit_MUX u_32bit_mux_1 (
    .in_1(n74157_1_p1), .Input_0(paddingmodule_2_out_3), .Input_1(paddingmodule_1_out_3),
    .Output(n32bit_mux_1_output));
  SignedSubtractor signedsubtractor_1 (
    .A_B(signedsubtractor_1_a_b), .MSB__isNeg(signedsubtractor_1_msb__isneg), .A(compareexp_1_larger_exp),
    .B(nomalizatonmodule_1_shamt));
  PaddingModule paddingmodule_2 (.Fraction(Number_B[20:0]), .Exponent(Number_B[30:21]), .out_3(paddingmodule_2_out_3));
  AlignModule alignmodule_1 (
    .Small_Significand_OUT(alignmodule_1_small_significand_out), .expdiff(compareexp_1_exponent_difference),
    .Small_Significand_IN(n32bit_mux_2_output));
  AdderModule addermodule_1 (
    .sign_L(n74157_1_p7), .sign_S(n74157_1_p4), .out_5(addermodule_1_out_5),
    .Large_Significand(n32bit_mux_1_output), .Small_significand(alignmodule_1_small_significand_out));
  _32bit_MUX u_32bit_mux_2 (
    .in_1(n74157_1_p1), .Input_0(paddingmodule_1_out_3), .Input_1(paddingmodule_2_out_3),
    .Output(n32bit_mux_2_output));
  NomalizatonModule nomalizatonmodule_1 (
    .FROM_ADDER_UNIT__Input(addermodule_1_out_5), .SHAMT(nomalizatonmodule_1_shamt),
    .Normalized_OP(nomalizatonmodule_1_normalized_op), .Sign(Rounded_Output[31]),
    .At_least_one_1(nomalizatonmodule_1_at_least_one_1));
  RoundingModule roundingmodule_1 (
    .SignificantOUT({roundingmodule_1_significantout[31:29], Rounded_Output[20:0], roundingmodule_1_significantout[7:0]}),
    .ExpOUT(Rounded_Output[30:21]), .ExpIN(signedsubtractor_1_a_b),
    .SignificantIN(nomalizatonmodule_1_normalized_op));
  // Probe on addermodule_1_out_5
  // Probe on nomalizatonmodule_1_normalized_op

  // Notes on the sheet:
  //   Sign S
  //   Sign L
  //   large
  //   normalized exp
  //   small
  //   rounded exp
  //   normalized xxxFractionxxx
endmodule

// Normalization
module NomalizatonModule (
  input  [31:0] FROM_ADDER_UNIT__Input,
  output [9:0] SHAMT,
  output At_least_one_1,
  output [31:0] Normalized_OP,
  output Sign
);

  wire [4:0] bitfinder_1_index;
  wire [9:0] subtractor_1_out;
  wire [31:0] n32bit_mux_1_output, negator_1_out, shifter_1_out;

  // Probe on FROM_ADDER_UNIT__Input
  _32bit_MUX u_32bit_mux_1 (
    .in_1(FROM_ADDER_UNIT__Input[31]), .Input_0(FROM_ADDER_UNIT__Input), .Input_1(negator_1_out),
    .Output(n32bit_mux_1_output));
  Negator #(.width(32)) negator_1 (.in(FROM_ADDER_UNIT__Input), .out(negator_1_out));
  // Probe on n32bit_mux_1_output
  // Probe on negator_1_out
  BitFinder #(.width(32)) bitfinder_1 (
    .in({1'b0, n32bit_mux_1_output[0], n32bit_mux_1_output[1], n32bit_mux_1_output[2], n32bit_mux_1_output[3], n32bit_mux_1_output[4], n32bit_mux_1_output[5], n32bit_mux_1_output[6], n32bit_mux_1_output[7], n32bit_mux_1_output[8], n32bit_mux_1_output[9], n32bit_mux_1_output[10], n32bit_mux_1_output[11], n32bit_mux_1_output[12], n32bit_mux_1_output[13], n32bit_mux_1_output[14], n32bit_mux_1_output[15], n32bit_mux_1_output[16], n32bit_mux_1_output[17], n32bit_mux_1_output[18], n32bit_mux_1_output[19], n32bit_mux_1_output[20], n32bit_mux_1_output[21], n32bit_mux_1_output[22], n32bit_mux_1_output[23], n32bit_mux_1_output[24], n32bit_mux_1_output[25], n32bit_mux_1_output[26], n32bit_mux_1_output[27], n32bit_mux_1_output[28], n32bit_mux_1_output[29], n32bit_mux_1_output[30]}),
    .index(bitfinder_1_index), .found(At_least_one_1));
  Subtractor #(.width(10)) subtractor_1 (
    .a({{5{1'b0}}, bitfinder_1_index}), .b({10{1'b0}}), .out(subtractor_1_out), .bin(1'b1));  // open: bout
  // Probe on shifter_1_out
  Shifter #(.width(32)) shifter_1 (.in(n32bit_mux_1_output), .\dist (bitfinder_1_index), .out(shifter_1_out));
  _10bit_MUX u_10bit_mux_1 (.s(At_least_one_1), .input_A({10{1'b0}}), .input_B(subtractor_1_out), .out_4(SHAMT));
  Shifter #(.width(32), .shift("lr")) shifter_2 (.in(shifter_1_out), .\dist (5'b00001), .out(Normalized_OP));

  assign Sign = FROM_ADDER_UNIT__Input[31];
endmodule

// AdderM
module AdderModule (
  input  [31:0] Large_Significand,
  input  sign_L,
  input  sign_S,
  input  [31:0] Small_significand,
  output [31:0] out_5
);

  wire [31:0] checksign_1_frac_out, checksign_2_frac_out;

  CheckSign checksign_1 (.frac_out(checksign_1_frac_out), .sign(sign_L), .frac_in(Large_Significand));
  CheckSign checksign_2 (.frac_out(checksign_2_frac_out), .sign(sign_S), .frac_in(Small_significand));
  Adder #(.width(32)) adder_1 (
    .a(checksign_1_frac_out), .b(checksign_2_frac_out), .out(out_5), .cin(1'b0));  // open: cout
endmodule

// Align M
module AlignModule (
  input  [31:0] Small_Significand_IN,
  input  [9:0] expdiff,
  output [31:0] Small_Significand_OUT
);

  wire n5bit_or_1_output;
  wire [31:0] shifter_1_out;

  _5bit_OR u_5bit_or_1 (
    .in_1(expdiff[5]), .in_2(expdiff[6]), .in_3(expdiff[7]), .in_4(expdiff[8]), .in_5(expdiff[9]),
    .\output (n5bit_or_1_output));
  Shifter #(.width(32), .shift("lr")) shifter_1 (.in(Small_Significand_IN), .\dist (expdiff[4:0]), .out(shifter_1_out));
  _32bit_MUX u_32bit_mux_1 (
    .in_1(n5bit_or_1_output), .Input_0(shifter_1_out), .Input_1({32{1'b0}}), .Output(Small_Significand_OUT));
endmodule

// Rounding M
module RoundingModule (
  input  [9:0] ExpIN,
  input  [31:0] SignificantIN,
  output [31:0] SignificantOUT,
  output [9:0] ExpOUT
);

  wire n6bit_or_1_output, n7408_1_p2, n7432_1_p4;
  wire [8:8] n7408_1_p3;
  wire [9:0] nomalizatonmodule_1_shamt;
  wire [31:0] adder_1_out;

  _6bit_OR u_6bit_or_1 (
    .in_1(SignificantIN[0]), .in_2(SignificantIN[1]), .in_3(SignificantIN[2]), .in_4(SignificantIN[3]),
    .in_5(SignificantIN[4]), .in_6(SignificantIN[5]), .\output (n6bit_or_1_output));
  // _7408 7408_1: pin names not known; wires that end beside it: SignificantIN[7], n7408_1_p2, n7408_1_p3[8], 1'b1
  // _7432 7432_1: pin names not known; wires that end beside it: 1'b0, n6bit_or_1_output, SignificantIN[6], n7432_1_p4, n7432_1_p4, SignificantIN[8], n7408_1_p2, 1'b0, 1'b1
  Subtractor #(.width(10)) subtractor_1 (
    .a(ExpIN), .b(nomalizatonmodule_1_shamt), .out(ExpOUT), .bin(1'b0));  // open: bout
  Adder #(.width(32)) adder_1 (
    .a({{23{1'b0}}, n7408_1_p3[8], {8{1'b0}}}), .b({SignificantIN[31:8], {8{1'b0}}}), .out(adder_1_out),
    .cin(1'b0));  // open: cout
  // Probe on adder_1_out
  NomalizatonModule nomalizatonmodule_1 (
    .FROM_ADDER_UNIT__Input(adder_1_out), .SHAMT(nomalizatonmodule_1_shamt), .Normalized_OP(SignificantOUT));  // open: Sign, At_least_one_1
endmodule

// Over/Under
module Overflow_Underflow (
  input  _11th_bit__From_exp_subt,
  input  At_least_one_1,
  input  [9:0] Normalized_exp,
  input  [9:0] Rounded_Exp,
  output Underflow,
  output Overflow
);

  wire n10bit_and_1_output, n10bit_and_2_output, n10bit_or_1_output, n7404_1_p2, n7408_1_p3;

  _10bit_OR u_10bit_or_1 (
    .in_1(Normalized_exp[0]), .in_2(Normalized_exp[1]), .in_3(Normalized_exp[2]), .in_4(Normalized_exp[3]),
    .in_5(Normalized_exp[4]), .in_6(Normalized_exp[5]), .in_7(Normalized_exp[6]), .in_8(Normalized_exp[7]),
    .in_9(Normalized_exp[8]), .in_10(Normalized_exp[9]), .\output (n10bit_or_1_output));
  _10bit_AND u_10bit_and_1 (
    .in_1(Normalized_exp[0]), .in_2(Normalized_exp[1]), .in_3(Normalized_exp[2]), .in_4(Normalized_exp[3]),
    .in_5(Normalized_exp[4]), .in_6(Normalized_exp[5]), .in_7(Normalized_exp[6]), .in_8(Normalized_exp[7]),
    .in_9(Normalized_exp[8]), .in_10(Normalized_exp[9]), .\output (n10bit_and_1_output));
  _10bit_AND u_10bit_and_2 (
    .in_1(Rounded_Exp[0]), .in_2(Rounded_Exp[1]), .in_3(Rounded_Exp[2]), .in_4(Rounded_Exp[3]),
    .in_5(Rounded_Exp[4]), .in_6(Rounded_Exp[5]), .in_7(Rounded_Exp[6]), .in_8(Rounded_Exp[7]),
    .in_9(Rounded_Exp[8]), .in_10(Rounded_Exp[9]), .\output (n10bit_and_2_output));
  // _7404 7404_1: pin names not known; wires that end beside it: n10bit_or_1_output, n7404_1_p2, 1'b0, 1'b1
  // _7408 7408_1: pin names not known; wires that end beside it: At_least_one_1, n7404_1_p2, n7408_1_p3, 1'b0, 1'b1
  // _7432 7432_1: pin names not known; wires that end beside it: _11th_bit__From_exp_subt, n7408_1_p3, Underflow, n10bit_and_1_output, n10bit_and_2_output, Overflow, 1'b0, 1'b1
endmodule

// SignExtendedSubtractor
module SignedSubtractor (
  input  [9:0] A,
  input  [9:0] B,
  output [9:0] A_B,
  output MSB__isNeg
);

  wire subtractor_1_bout;

  Subtractor #(.width(10)) subtractor_1 (.a(A), .b(B), .out(A_B), .bout(subtractor_1_bout));  // open: bin
  Subtractor #(.width(1)) subtractor_2 (.a(1'b0), .b(B[9]), .out(MSB__isNeg), .bin(subtractor_1_bout));  // open: bout
endmodule

module _10bit_OR (
  input  in_1,
  input  in_2,
  input  in_3,
  input  in_4,
  input  in_5,
  input  in_6,
  input  in_7,
  input  in_8,
  input  in_9,
  input  in_10,
  output \output 
);

  wire n7432_1_p3, n7432_1_p6, n7432_1_p11, n7432_1_p14, n7432_2_p3, n7432_2_p6, n7432_2_p10, n7432_2_p13;

  // _7432 7432_1: pin names not known; wires that end beside it: in_1, in_2, n7432_1_p3, n7432_1_p3, in_3, n7432_1_p6, 1'b0, 1'b1, n7432_1_p6, in_4, n7432_1_p11, n7432_1_p11, in_5, n7432_1_p14
  // _7432 7432_2: pin names not known; wires that end beside it: n7432_1_p14, in_6, n7432_2_p3, n7432_2_p3, in_7, n7432_2_p6, 1'b0, n7432_2_p6, in_8, n7432_2_p10, n7432_2_p10, in_9, n7432_2_p13
  // _7432 7432_3: pin names not known; wires that end beside it: n7432_2_p13, in_10, \output , 1'b0
endmodule

module _5bit_OR (
  input  in_1,
  input  in_2,
  input  in_3,
  input  in_4,
  input  in_5,
  output \output 
);

  wire n7432_1_p3, n7432_1_p6, n7432_1_p11;

  // _7432 7432_1: pin names not known; wires that end beside it: in_1, in_2, n7432_1_p3, n7432_1_p3, in_3, n7432_1_p6, 1'b0, 1'b1, n7432_1_p6, in_4, n7432_1_p11, n7432_1_p11, in_5, \output 
endmodule

module _10bit_AND (
  input  in_1,
  input  in_2,
  input  in_3,
  input  in_4,
  input  in_5,
  input  in_6,
  input  in_7,
  input  in_8,
  input  in_9,
  input  in_10,
  output \output 
);

  wire n7408_1_p3, n7408_1_p6, n7408_1_p11, n7408_1_p14, n7408_2_p3, n7408_2_p6, n7408_2_p10, n7408_2_p13;

  // _7408 7408_1: pin names not known; wires that end beside it: in_1, in_2, n7408_1_p3, n7408_1_p3, in_3, n7408_1_p6, 1'b0, 1'b1, n7408_1_p6, in_4, n7408_1_p11, n7408_1_p11, in_5, n7408_1_p14
  // _7408 7408_2: pin names not known; wires that end beside it: n7408_1_p14, in_6, n7408_2_p3, n7408_2_p3, in_7, n7408_2_p6, 1'b0, n7408_2_p6, in_8, n7408_2_p10, n7408_2_p10, in_9, n7408_2_p13
  // _7408 7408_3: pin names not known; wires that end beside it: n7408_2_p13, in_10, \output , 1'b0
endmodule

// 32bit MUX
module _32bit_MUX (
  input  in_1,
  input  [31:0] Input_0,
  input  [31:0] Input_1,
  output [31:0] Output
);

  // _74157 74157_1: pin names not known; wires that end beside it: in_1, Input_0[0], Input_1[0], Output[0], Input_0[1], Input_1[1], Output[1], 1'b0, 1'b1, 1'b0, Input_0[2], Input_1[2], Output[2], Input_0[3], Input_1[3], Output[3]
  // _74157 74157_2: pin names not known; wires that end beside it: in_1, Input_0[4], Input_1[4], Output[4], Input_0[5], Input_1[5], Output[5], 1'b0, 1'b1, 1'b0, Input_0[6], Input_1[6], Output[6], Input_0[7], Input_1[7], Output[7]
  // _74157 74157_3: pin names not known; wires that end beside it: in_1, Input_0[8], Input_1[8], Output[8], Input_0[9], Input_1[9], Output[9], 1'b0, 1'b1, 1'b0, Input_0[10], Input_1[10], Output[10], Input_0[11], Input_1[11], Output[11]
  // _74157 74157_4: pin names not known; wires that end beside it: in_1, Input_0[12], Input_1[12], Output[12], Input_0[13], Input_1[13], Output[13], 1'b0, 1'b1, 1'b0, Input_0[14], Input_1[14], Output[14], Input_0[15], Input_1[15], Output[15]
  // _74157 74157_5: pin names not known; wires that end beside it: in_1, Input_0[16], Input_1[16], Output[16], Input_0[17], Input_1[17], Output[17], 1'b0, 1'b1, 1'b0, Input_0[18], Input_1[18], Output[18], Input_0[19], Input_1[19], Output[19]
  // _74157 74157_6: pin names not known; wires that end beside it: in_1, Input_0[20], Input_1[20], Output[20], Input_0[21], Input_1[21], Output[21], 1'b0, 1'b1, 1'b0, Input_0[22], Input_1[22], Output[22], Input_0[23], Input_1[23], Output[23]
  // _74157 74157_7: pin names not known; wires that end beside it: in_1, Input_0[24], Input_1[24], Output[24], Input_0[25], Input_1[25], Output[25], 1'b0, 1'b1, 1'b0, Input_0[26], Input_1[26], Output[26], Input_0[27], Input_1[27], Output[27]
  // _74157 74157_8: pin names not known; wires that end beside it: in_1, Input_0[28], Input_1[28], Output[28], Input_0[29], Input_1[29], Output[29], 1'b0, 1'b1, 1'b0, Input_0[31], Input_1[31], Output[31], Input_0[30], Input_1[30], Output[30]
endmodule

module _6bit_OR (
  input  in_1,
  input  in_2,
  input  in_3,
  input  in_4,
  input  in_5,
  input  in_6,
  output \output 
);

  wire n7432_1_p3, n7432_1_p6, n7432_1_p11, n7432_1_p14;

  // _7432 7432_1: pin names not known; wires that end beside it: in_1, in_2, n7432_1_p3, n7432_1_p3, in_3, n7432_1_p6, 1'b0, 1'b1, n7432_1_p6, in_4, n7432_1_p11, n7432_1_p11, in_5, n7432_1_p14
  // _7432 7432_2: pin names not known; wires that end beside it: n7432_1_p14, in_6, \output , 1'b0, 1'b1
endmodule

module _10bit_MUX (
  input  s,
  input  [9:0] input_A,
  input  [9:0] input_B,
  output [9:0] out_4
);

  // _74157 74157_1: pin names not known; wires that end beside it: s, input_A[0], input_B[0], out_4[0], input_A[1], input_B[1], out_4[1], 1'b0, 1'b1, 1'b0, input_A[2], input_B[2], out_4[2], input_A[3], input_B[3], out_4[3]
  // _74157 74157_2: pin names not known; wires that end beside it: s, input_A[4], input_B[4], out_4[4], input_A[5], input_B[5], out_4[5], 1'b0, 1'b1, 1'b0, input_A[6], input_B[6], out_4[6], input_A[7], input_B[7], out_4[7]
  // _74157 74157_3: pin names not known; wires that end beside it: s, input_A[8], input_B[8], out_4[8], input_A[9], input_B[9], out_4[9], 1'b0, 1'b1, 1'b0

  // Notes on the sheet:
  //   s=0 -> select input A
  //   s=1 -> select input B
endmodule
