// Logisim project circuit_simulation.circ as structural Verilog: 6 circuits, main circuit main
module main (
  input  pc_reset,
  output [3:0] ZERO,
  output [3:0] t0,
  output [3:0] t1,
  output [3:0] t2,
  output [3:0] t3,
  output [3:0] t4,
  output [3:0] sp
);

  wire alu_module_1_zf, clock_1_out, control_unit_module_1_alusrc, control_unit_module_1_beq,
       control_unit_module_1_bneq, control_unit_module_1_jump, control_unit_module_1_memread,
       control_unit_module_1_memtoreg, control_unit_module_1_memwrite, control_unit_module_1_regdst,
       control_unit_module_1_regwrite, register_file_module_1_readsp;
  wire [2:0] control_unit_module_1_aluop;
  wire [3:0] alu_module_1_s, data_memory_module_1_data_out, multiplexer_1_out, multiplexer_2_out,
       multiplexer_3_out, register_file_module_1_readdata1, register_file_module_1_readdata2;
  wire [7:0] pc_handle_module_1_to_pc, PC_q;
  wire [15:0] ins_memory_data;

  Clock clock_1 (.out(clock_1_out));
  Register PC (.D(pc_handle_module_1_to_pc), .en(1'b1), .clk(clock_1_out), .Q(PC_q), .clr(pc_reset));
  ROM #(.dataWidth(16)) ins_memory (.addr(PC_q), .data(ins_memory_data));
  control_unit_module control_unit_module_1 (
    .in_1(ins_memory_data[15:12]), .ALUsrc(control_unit_module_1_alusrc),
    .ALUop(control_unit_module_1_aluop), .BEQ(control_unit_module_1_beq), .BNEQ(control_unit_module_1_bneq),
    .JUMP(control_unit_module_1_jump), .RegDst(control_unit_module_1_regdst),
    .RegWrite(control_unit_module_1_regwrite), .MemRead(control_unit_module_1_memread),
    .MemWrite(control_unit_module_1_memwrite), .MemToReg(control_unit_module_1_memtoreg));
  Multiplexer #(.width(4)) multiplexer_1 (
    .in0(ins_memory_data[7:4]), .in1(ins_memory_data[3:0]), .out(multiplexer_1_out),
    .sel(control_unit_module_1_regdst));
  pc_handle_module pc_handle_module_1 (
    .ZF(alu_module_1_zf), .from_pc(PC_q), .beq(control_unit_module_1_beq), .bneq(control_unit_module_1_bneq),
    .jump(control_unit_module_1_jump), .JumpAddr(ins_memory_data[11:4]), .ins_offset(ins_memory_data[3:0]),
    .to_pc(pc_handle_module_1_to_pc));
  register_file_module register_file_module_1 (
    .RegWrite(control_unit_module_1_regwrite), .WriteData(multiplexer_3_out),
    .WriteRegister(multiplexer_1_out), .ReadRegister1(ins_memory_data[11:8]),
    .ReadRegister2(ins_memory_data[7:4]), .CLK(clock_1_out), .regs({sp, t4, t3, t2, t1, t0, ZERO}),
    .ReadData1(register_file_module_1_readdata1), .ReadData2(register_file_module_1_readdata2),
    .ReadSP(register_file_module_1_readsp));
  Multiplexer #(.width(4)) multiplexer_2 (
    .in0(register_file_module_1_readdata2), .in1(ins_memory_data[3:0]), .out(multiplexer_2_out),
    .sel(control_unit_module_1_alusrc));
  alu_module alu_module_1 (
    .A(register_file_module_1_readdata1), .B(multiplexer_2_out), .ALUop(control_unit_module_1_aluop),
    .S(alu_module_1_s), .ZF(alu_module_1_zf));
  data_memory_module data_memory_module_1 (
    .address(alu_module_1_s), .data_in(register_file_module_1_readdata2),
    .read_enable(control_unit_module_1_memread), .write_enable(control_unit_module_1_memwrite),
    .is_stack(register_file_module_1_readsp), .CLK(clock_1_out), .data_out(data_memory_module_1_data_out));
  Multiplexer #(.width(4)) multiplexer_3 (
    .in0(alu_module_1_s), .in1(data_memory_module_1_data_out), .out(multiplexer_3_out),
    .sel(control_unit_module_1_memtoreg));

  // Notes on the sheet:
  //   contents of ins_memory (hex, n*v repeats v):
  //   9015 9023 8212 5242
endmodule

module data_memory_module (
  input  [3:0] address,
  input  [3:0] data_in,
  input  read_enable,
  input  write_enable,
  input  is_stack,
  input  CLK,
  output [3:0] data_out
);

  wire and_1_out, and_2_out, not_1_out;
  wire [3:0] data_memory_dout, stack_dout;

  not not_1 (not_1_out, is_stack);
  and and_1 (and_1_out, write_enable, not_1_out);
  and and_2 (and_2_out, is_stack, write_enable);
  RAM #(.addrWidth(4), .dataWidth(4), .enables("line")) data_memory (
    .addr(address), .we(and_1_out), .oe(read_enable), .clk(CLK), .din(data_in), .dout(data_memory_dout));
  RAM #(.addrWidth(4), .clearpin("true"), .dataWidth(4), .enables("line")) stack (
    .addr(address), .we(and_2_out), .oe(read_enable), .clk(CLK), .din(data_in), .dout(stack_dout));  // open: clr
  Multiplexer #(.width(4)) multiplexer_1 (.in0(data_memory_dout), .in1(stack_dout), .out(data_out), .sel(is_stack));
endmodule

module register_file_module (
  input  RegWrite,
  input  [3:0] WriteData,
  input  [3:0] WriteRegister,
  input  [3:0] ReadRegister1,
  input  [3:0] ReadRegister2,
  input  CLK,
  output [27:0] regs,
  output [3:0] ReadData1,
  output [3:0] ReadData2,
  output ReadSP
);

  wire decoder_1_out1, decoder_1_out2, decoder_1_out3, decoder_1_out4, decoder_1_out5, decoder_1_out6,
       not_1_out;

  Decoder #(.select(3)) decoder_1 (
    .out1(decoder_1_out1), .out2(decoder_1_out2), .out3(decoder_1_out3), .out4(decoder_1_out4),
    .out5(decoder_1_out5), .out6(decoder_1_out6), .sel(WriteRegister[2:0]), .en(RegWrite));  // open: out0, out7
  Register #(.width(4)) zero (.clk(CLK), .Q(regs[3:0]), .clr(1'b1));  // open: D, en
  Register #(.width(4)) t0 (.D(WriteData), .en(decoder_1_out1), .clk(CLK), .Q(regs[7:4]));  // open: clr
  Register #(.width(4)) t1 (.D(WriteData), .en(decoder_1_out2), .clk(CLK), .Q(regs[11:8]));  // open: clr
  Register #(.width(4)) t2 (.D(WriteData), .en(decoder_1_out3), .clk(CLK), .Q(regs[15:12]));  // open: clr
  Register #(.width(4)) t3 (.D(WriteData), .en(decoder_1_out4), .clk(CLK), .Q(regs[19:16]));  // open: clr
  Register #(.width(4)) t4 (.D(WriteData), .en(decoder_1_out5), .clk(CLK), .Q(regs[23:20]));  // open: clr
  Register #(.width(4)) sp (.D(WriteData), .en(decoder_1_out6), .clk(CLK), .Q(regs[27:24]));  // open: clr
  not not_1 (not_1_out, ReadRegister1[0]);
  and and_1 (ReadSP, not_1_out, ReadRegister1[1], ReadRegister1[2]);
  Multiplexer #(.select(3), .width(4)) multiplexer_1 (
    .in0(regs[3:0]), .in1(regs[7:4]), .in2(regs[11:8]), .in3(regs[15:12]), .in4(regs[19:16]),
    .in5(regs[23:20]), .in6(regs[27:24]), .out(ReadData1), .sel(ReadRegister1[2:0]));  // open: in7
  Multiplexer #(.select(3), .width(4)) multiplexer_2 (
    .in0(regs[3:0]), .in1(regs[7:4]), .in2(regs[11:8]), .in3(regs[15:12]), .in4(regs[19:16]),
    .in5(regs[23:20]), .in6(regs[27:24]), .out(ReadData2), .sel(ReadRegister2[2:0]));  // open: in7
endmodule

module alu_module (
  input  [3:0] A,
  input  [3:0] B,
  input  [2:0] ALUop,
  output [3:0] S,
  output ZF
);

  wire or_2_out, or_3_out;
  wire [3:0] adder_1_out, and_1_out, multiplexer_1_out, multiplexer_2_out, nor_1_out, or_1_out,
       shifter_1_out, shifter_2_out, subtractor_1_out;

  Adder #(.width(4)) adder_1 (.a(A), .b(B), .out(adder_1_out), .cin(1'b0));  // open: cout
  Subtractor #(.width(4)) subtractor_1 (.a(A), .b(B), .out(subtractor_1_out), .bin(1'b0));  // open: bout
  assign and_1_out = A & B;  // AND_Gate and_1, 4 bits wide
  assign or_1_out = A | B;  // OR_Gate or_1, 4 bits wide
  assign nor_1_out = ~(A | B);  // NOR_Gate nor_1, 4 bits wide
  Shifter #(.width(4)) shifter_1 (.in(A), .\dist (B[1:0]), .out(shifter_1_out));
  or or_2 (or_2_out, B[2], B[3]);
  Shifter #(.shift("lr"), .width(4)) shifter_2 (.in(A), .\dist (B[1:0]), .out(shifter_2_out));
  or or_3 (or_3_out, B[2], B[3]);
  Multiplexer #(.width(4)) multiplexer_1 (.in0(shifter_1_out), .in1(4'b0000), .out(multiplexer_1_out), .sel(or_2_out));
  Multiplexer #(.width(4)) multiplexer_2 (.in0(shifter_2_out), .in1(4'b0000), .out(multiplexer_2_out), .sel(or_3_out));
  Multiplexer #(.select(3), .width(4)) multiplexer_3 (
    .in0(adder_1_out), .in1(subtractor_1_out), .in2(and_1_out), .in3(or_1_out), .in4(nor_1_out),
    .in5(multiplexer_1_out), .in6(multiplexer_2_out), .out(S), .sel(ALUop));  // open: in7
  nor nor_2 (ZF, S[0], S[1], S[2], S[3]);
endmodule

module pc_handle_module (
  input  ZF,
  input  [7:0] from_pc,
  input  beq,
  input  bneq,
  input  jump,
  input  [7:0] JumpAddr,
  input  [3:0] ins_offset,
  output [7:0] to_pc
);

  wire and_1_out, and_2_out, not_1_out;
  wire [1:0] priority_encoder_1_out;
  wire [7:0] adder_1_out, adder_2_out, bit_extender_1_out;

  assign bit_extender_1_out = {{4{ins_offset[3]}}, ins_offset};  // Bit_Extender bit_extender_1
  not not_1 (not_1_out, ZF);
  and and_1 (and_1_out, beq, ZF);
  and and_2 (and_2_out, not_1_out, bneq);
  Adder adder_1 (.a(from_pc), .b(8'h1), .out(adder_1_out));  // open: cin, cout
  Adder adder_2 (.a(adder_1_out), .b(bit_extender_1_out), .out(adder_2_out));  // open: cin, cout
  Priority_Encoder #(.select(2)) priority_encoder_1 (
    .in0(1'b1), .in1(and_1_out), .in2(and_2_out), .in3(jump), .out(priority_encoder_1_out));  // open: gs, en_out, en_in
  Multiplexer #(.select(2), .width(8)) multiplexer_1 (
    .in0(adder_1_out), .in1(adder_2_out), .in2(adder_2_out), .in3(JumpAddr), .out(to_pc),
    .sel(priority_encoder_1_out));
endmodule

module control_unit_module (
  input  [3:0] in_1,
  output ALUsrc,
  output [2:0] ALUop,
  output BEQ,
  output BNEQ,
  output JUMP,
  output RegDst,
  output RegWrite,
  output MemRead,
  output MemWrite,
  output MemToReg
);

  ROM #(.addrWidth(4), .dataWidth(12)) rom_1 (
    .addr(in_1), .data({MemToReg, MemWrite, MemRead, RegWrite, RegDst, JUMP, BNEQ, BEQ, ALUop, ALUsrc}));

  // Notes on the sheet:
  //   contents of rom_1 (hex, n*v repeats v):
  //   186 103 107 182 180 b01 40 10b 401 101 10d 12 188 184 105 22
endmodule
